# Fritzing sketch schema (saved by Fritzing 0.9.3b)
breadboards: 1

parts:
  Part1 = Arduino Uno (Rev3)
  R1 = PHOTOCELL [package=photocell]
  LED1 = LED - 5mm [color="White (8000K)" package="5 mm [THT]"]
  R2 = Resistor [tolerance=±5% resistance=100 package="0402 [SMD]"]
  R3 = Resistor [tolerance=±5% resistance=10k package=THT]
  M1 = DC Motor
  Part2 = Bluetooth HC-05 Macho
  Part3 = Bluetooth HC-05 Macho

nets:
  N1: Part1.A0, R1.P$2, R3.Pin_0
  N2: Part1.D10_PWM/SS, Part2.TXD
  N3: Part1.D11_PWM/MOSI, Part2.RXD
  N4: Part1.D12/MISO, Part3.TXD
  N5: Part1.D13/SCK, Part3.RXD
  N6: Part1.D2, M1.pin_2
  N7: Part1.D4, M1.pin_1
  N8: Part1.D7, R2.Pin_0
  VCC: Part1.5V, R1.P$1, LED1.anode, Part2.VCC, Part3.VCC
  GND: Part1.GND, R3.Pin_1, Part2.GND, Part3.GND
  N9: LED1.cathode, R2.Pin_1
