# Fritzing sketch schema (saved by Fritzing 0.9.3b)
breadboards: 1

parts:
  Part1 = Arduino Uno (Rev3)
  R1 = PHOTOCELL [package=photocell]
  LED1 = LED - 5mm [color="Red (633nm)" package="5 mm [THT]"]
  R2 = Resistor [tolerance=±5% resistance=220 package="0402 [SMD]"]
  R3 = Resistor [tolerance=±5% resistance=220 package=THT]
  M1 = DC Motor
  Part2 = Bluetooth HC-05 Macho  # not connected

nets:
  N1: Part1.A0, R1.P$2, R3.Pin_0
  N2: Part1.D2, M1.pin_1
  N3: Part1.D4, M1.pin_2
  N4: Part1.D7, R2.Pin_0
  N5: Part1.5V, R1.P$1, LED1.cathode
  N6: Part1.GND, R3.Pin_1
  N7: LED1.anode, R2.Pin_1
